# Fritzing sketch Schematic (saved by Fritzing 0.9.3b)

parts:
  RGB_SMD_LED2 = SMD RGB LED (WS2812) [package=5050]
  RGB_SMD_LED3 = SMD RGB LED (WS2812) [package=5050]
  RGB_SMD_LED4 = SMD RGB LED (WS2812) [package=5050]
  RGB_SMD_LED5 = SMD RGB LED (WS2812) [package=5050]
  Part1 = Arduino Nano (Rev3.0) (ICSP)
  Part2 = Thumb Joystick

nets:
  N1: RGB_SMD_LED2.DOut, RGB_SMD_LED3.DIn
  N2: RGB_SMD_LED2.DIn, RGB_SMD_LED5.DOut
  VCC: RGB_SMD_LED2.VCC, RGB_SMD_LED3.VCC, RGB_SMD_LED4.VCC, RGB_SMD_LED5.VCC, Part1.5V, Part2.VCC
  N3: RGB_SMD_LED2.NC, RGB_SMD_LED3.NC
  N4: RGB_SMD_LED3.DOut, RGB_SMD_LED4.DIn
  GND: RGB_SMD_LED4.NC, RGB_SMD_LED5.NC, Part1.GND, Part2.GND
  N5: RGB_SMD_LED5.DIn, Part1.D5
  N6: Part1.D3, Part2.SEL
  N7: Part1.A2, Part2.HORZ
  N8: Part1.A0, Part2.VERT
